// Logisim project tiny8cpu.circ as structural Verilog: 1 circuit, main circuit main
module main (
);

  wire and_1_out, clock_1_out, comparator_1_eq, not_1_out, not_2_out, or_1_out;
  wire [1:0] and_3_out;
  wire [6:0] counter_1_q;
  wire [7:0] A_q, adder_1_out, B_q, ControlRom_data, multiplexer_1_out, multiplexer_2_out,
       programMemory_data, ram_1_dout, xor_1_out;

  Counter #(.max('h7f), .width(7)) counter_1 (
    .load(and_1_out), .count(or_1_out), .clk(clock_1_out), .D(programMemory_data[6:0]), .Q(counter_1_q));  // open: clr, up, carry
  ROM #(.addrWidth(3)) ControlRom (.addr(programMemory_data[6:4]), .data(ControlRom_data));
  Clock clock_1 (.out(clock_1_out));
  and and_1 (and_1_out, programMemory_data[7], comparator_1_eq);
  ROM #(.addrWidth(7)) programMemory (.addr(counter_1_q), .data(programMemory_data));
  Comparator comparator_1 (.a(A_q), .b({8{1'b0}}), .eq(comparator_1_eq));  // open: gt, lt
  RAM #(.addrWidth(4), .asyncread("true")) ram_1 (
    .addr(programMemory_data[3:0]), .we(ControlRom_data[3]), .oe(ControlRom_data[4]), .clk(clock_1_out),
    .din(A_q), .dout(ram_1_dout));
  or or_1 (or_1_out, programMemory_data[7], ControlRom_data[0]);
  and and_2 (and_3_out[1], not_1_out, not_2_out, ControlRom_data[4]);
  not not_1 (not_1_out, ControlRom_data[1]);
  not not_2 (not_2_out, ControlRom_data[2]);
  // Probe on A_q
  // Probe on B_q
  Multiplexer #(.select(2), .width(8)) multiplexer_1 (
    .in0({{5{programMemory_data[3]}}, programMemory_data[2:0]}), .in1(multiplexer_2_out), .in2(ram_1_dout),
    .out(multiplexer_1_out), .sel(and_3_out));  // open: in3
  and and_3 (and_3_out[0], not_1_out, ControlRom_data[2]);
  Register A (.D(multiplexer_1_out), .en(ControlRom_data[7]), .clk(clock_1_out), .Q(A_q));  // open: clr
  Register B (.D(ram_1_dout), .en(ControlRom_data[6]), .clk(clock_1_out), .Q(B_q));  // open: clr
  Adder adder_1 (.a(A_q), .b(B_q), .out(adder_1_out));  // open: cin, cout
  assign xor_1_out = A_q ^ B_q;  // XOR_Gate xor_1, 8 bits wide
  Multiplexer #(.width(8)) multiplexer_2 (
    .in0(adder_1_out), .in1(xor_1_out), .out(multiplexer_2_out), .sel(ControlRom_data[5]));

  // Notes on the sheet:
  //   contents of ControlRom (hex, n*v repeats v):
  //   0 83 91 51 9 85 a5
  //   contents of programMemory (hex, n*v repeats v):
  //   1f 40 15 41 30 55 55 42 22 a0 21 43 22 44 24 9a 21 33 55 41 24 30 55 44 10 8e 22 30 55 42 10 88 21 0
  //   4 8 21
endmodule
